# Fritzing sketch flem 420 pcb brief2 (saved by Fritzing 0.9.3b)
circuit board: 1.65329cm x 2.25821cm
circuit board: 3.85727cm x 3.35037cm
breadboards: 1

parts:
  O/I = Toggle Switch [package=THT]
  Mini = Arduino Pro Mini (3.3V)
  OLED = female pin header, 4 pins [form="♀ (female)"]
  V_G = female pin header, 2 pins [form="♀ (female)"]
  VGLA = female pin header, 4 pins [form="♀ (female)"]
  part = female pin header, 4 pins [form="♀ (female)"]
  B1m = Pushbutton [package="[THT]"]
  B2 = Pushbutton [package="[THT]"]
  R10k2 = Resistor [tolerance=±5% resistance=220 package=THT]
  R10k1 = Resistor [tolerance=±5% resistance=220 package=THT]
  VD4_D3_G = female pin header, 4 pins [form="♀ (female)"]

nets (from the pcb view):
  N1: O/I.L1, V_G.pin2
  N2: O/I.COM, Mini.RAW, OLED.pin2, VGLA.pin1, part.pin4
  N3: Mini.GND, OLED.pin1, V_G.pin1, VGLA.pin2, part.pin1
  N4: Mini.A4, OLED.pin4, VGLA.pin4
  N5: Mini.A5, OLED.pin3, VGLA.pin3
  N6: Mini.D4, part.pin3
  N7: Mini.D3, part.pin2
  N8: B1m.Pin_1, B1m.Pin_2, R10k1.Pin_0, VD4_D3_G.pin2
  N9: B1m.Pin_3, B1m.Pin_4, B2.Pin_4, VD4_D3_G.pin4
  N10: B2.Pin_1, B2.Pin_2, R10k2.Pin_0, VD4_D3_G.pin3
  N11: R10k2.Pin_1, R10k1.Pin_1, VD4_D3_G.pin1

notes:
  A5 A4
  SCL
  SDA
  Btns
  VD4D3G
  GVLA
  BMP
